# Fritzing sketch Estim_Circuit_Diagram (saved by Fritzing 1.0.1rc)
breadboards: 2

parts:
  U1 = ESP32-38PinWide [part_number=ESP32-38PinWide]
  R1 = Resistor [tolerance=±5% power=0.25W resistance=10 package=THT]
  R2 = Resistor [tolerance=±5% power=0.25W resistance=10 package=THT]
  R4 = Resistor [tolerance=±5% power=0.25W resistance=10 package=THT]
  R5 = Resistor [tolerance=±5% power=0.25W resistance=10 package=THT]
  R6 = Resistor [tolerance=±5% power=0.25W resistance=10 package=THT]
  R7 = Resistor [tolerance=±5% power=0.25W resistance=10 package=THT]
  R8 = Resistor [tolerance=±5% power=0.25W resistance=10 package=THT]
  R9 = Resistor [tolerance=±5% power=0.25W resistance=10 package=THT]
  U2 = 74HC4051 [package=so16]
  R10 = Resistor [tolerance=±5% power=0.25W resistance=1M package=THT]
  R11 = Resistor [tolerance=±5% power=0.25W resistance=1M package=THT]
  R12 = Resistor [tolerance=±5% power=0.25W resistance=1M package=THT]
  R13 = Resistor [tolerance=±5% power=0.25W resistance=1M package=THT]
  R14 = Resistor [tolerance=±5% power=0.25W resistance=1M package=THT]
  R15 = Resistor [tolerance=±5% power=0.25W resistance=1M package=THT]
  R16 = Resistor [tolerance=±5% power=0.25W resistance=1M package=THT]
  R17 = Resistor [tolerance=±5% power=0.25W resistance=1M package=THT]
  R21 = Resistor [tolerance=±5% power=0.25W resistance=270k package=THT]
  R22 = Resistor [tolerance=±5% power=0.25W resistance=270k package=THT]
  R23 = Resistor [tolerance=±5% power=0.25W resistance=270k package=THT]
  R24 = Resistor [tolerance=±5% power=0.25W resistance=270k package=THT]
  R25 = Resistor [tolerance=±5% power=0.25W resistance=270k package=THT]
  R26 = Resistor [tolerance=±5% power=0.25W resistance=270k package=THT]
  R27 = Resistor [tolerance=±5% power=0.25W resistance=270k package=THT]
  R28 = Resistor [tolerance=±5% power=0.25W resistance=270k package=THT]
  IC1 = L293D [package=THT]
  microSD1 = MicroSD Card Module
  J1 = Piezo Speaker
  R29 = Resistor [tolerance=±5% power=0.25W resistance=100 package=THT]
  LED1 = LED - 5mm [color="Red (633nm)" current=0.030A package="5 mm [THT]"]
  R30 = Resistor [tolerance=±5% power=0.25W resistance=270 package=THT]
  R31 = Resistor [tolerance=±5% power=0.25W resistance=1M package=THT]
  R32 = Resistor [tolerance=±5% power=0.25W resistance=1M package=THT]
  R33 = Resistor [tolerance=±5% power=0.25W resistance=270k package=THT]
  R34 = Resistor [tolerance=±5% power=0.25W resistance=270k package=THT]
  M1 = RioRand LM2596
  VM1 = Voltmeter (3 wire)

nets:
  N1: U1.GPIO36, R10.Pin_0, R28.Pin_1
  N2: U1.GPIO39, R11.Pin_0, R27.Pin_1
  N3: U1.GPIO34, U2.IO
  N4: U1.GPIO32, R31.Pin_0, R33.Pin_1
  N5: U1.GPIO33, R32.Pin_0, R34.Pin_1
  N6: U1.GPIO26, LED1.cathode
  N7: U1.GPIO27, U2.A
  N8: U1.GPIO14, U2.B
  N9: U1.GPIO13, U2.C
  GND: U1.GPIO11, U2.INH, U2.VEE, U2.VSS, R21.Pin_0, R22.Pin_0, R23.Pin_0, R24.Pin_0, R25.Pin_0, R26.Pin_0, R27.Pin_0, R28.Pin_0, IC1.0V, microSD1.GND, J1.pin1, R30.Pin_0, R33.Pin_0, R34.Pin_0, M1.Pin_4, VM1.GND
  VCC: U1.VIN, U2.VDD, IC1.Enable_1, IC1.+V, microSD1.VCC, VM1.VCC
  N10: U1.GPIO4, R29.Pin_0
  N11: U1.GPIO5, microSD1.CS
  N12: U1.GPIO18, microSD1.SCK
  N13: U1.GPIO19, microSD1.MISO
  N14: U1.GPIO21, IC1.In_1
  N15: U1.GPIO22, IC1.In_2
  N16: U1.GPIO23, microSD1.MOSI
  N17: R1.Pin_0, R10.Pin_1
  N18: R1.Pin_1, R4.Pin_1, R6.Pin_1, R8.Pin_1, R17.Pin_1, IC1.Out_1_(_Controlled_by_Enable_1_), R32.Pin_1
  N19: R2.Pin_0, R11.Pin_1
  N20: R2.Pin_1, R5.Pin_1, R7.Pin_1, R9.Pin_1, R16.Pin_1, IC1.Out_2_(_Controlled_by_Enable_1_), R31.Pin_1
  N21: R4.Pin_0, R13.Pin_1
  N22: R5.Pin_0, R12.Pin_1
  N23: R6.Pin_0, R15.Pin_1
  N24: R7.Pin_0, R14.Pin_1
  N25: U2.IO4, R16.Pin_0, R25.Pin_1
  N26: U2.IO6, R17.Pin_0, R24.Pin_1
  N27: U2.IO7, R15.Pin_0, R22.Pin_1
  N28: U2.IO5, R14.Pin_0, R23.Pin_1
  N29: U2.IO0, R13.Pin_0, R26.Pin_1
  N30: U2.IO1, R12.Pin_0, R21.Pin_1
  N31: IC1.+Vmotor, M1.Pin_3, VM1.Vin
  N32: J1.pin2, R29.Pin_1
  N33: LED1.anode, R30.Pin_1

custom parts:
  ESP32-38PinWide: Generic 38-Pin ESP32 with wide format (only access to one side of pins on a breadboard) based on Stephen Lilley's HiLetgo ESP-WROOM-32 ESP32 ESP-32S Development Board.
  Voltmeter (3 wire): Voltmeter, 3 digit LED (.56 inch) output, 3 wire (Power 3.5V to 30V, Ground, Vin) comes in several colors (red, green, orange, blue). Available from Ebay and Amazon and others, no bezel (although bezels to fit them are currently available on Ebay). The mounting ears on what you get may or may not be the same as the ones I have. Won't run on 3.3V so you would need a 5 volt source or a 3V to 5V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
